// Logisim project main.circ as structural Verilog
module mips (
  input  reset
);

  wire clk;

  Clock clock_1 (.out(clk));
  DataPath datapath_1 ();  // open: clk, reset, sign, WeGrf, branch, WeDm, JType, jr, RegDst, WhichtoReg, AluSrc, AluOp, instr
  Controller controller_1 ();  // open: AluOp, WeGrf, WeDm, branch, AluSrc, WhichtoReg, RegDst, sign, JType, jr, instr, eq

  // Notes on the sheet:
  //   MIPS
endmodule

module Controller (
  input  [31:0] instr,
  input  eq,
  output WeGrf,
  output WeDm,
  output [1:0] RegDst,
  output [1:0] WhichtoReg,
  output AluSrc,
  output [2:0] AluOp,
  output sign,
  output branch,
  output JType,
  output jr
);

  wire addu, beq, j, jal, lui, lw, not_1_out, not_2_out, not_3_out, not_4_out, not_5_out, not_6_out,
       not_7_out, not_8_out, not_9_out, not_10_out, not_11_out, not_12_out, ori, R, subu;

  // Probe on instr[31:26]
  not not_1 (not_1_out, instr[29]);
  not not_2 (not_2_out, instr[30]);
  not not_3 (not_3_out, instr[31]);
  not not_4 (not_4_out, instr[28]);
  not not_5 (not_5_out, instr[26]);
  not not_6 (not_6_out, instr[27]);
  // Probe on instr[5:0]
  not not_7 (not_7_out, instr[5]);
  not not_8 (not_8_out, instr[4]);
  not not_9 (not_9_out, instr[3]);
  not not_10 (not_10_out, instr[2]);
  not not_11 (not_11_out, instr[1]);
  not not_12 (not_12_out, instr[0]);
  and u_R (R, not_5_out, not_6_out, not_4_out, not_1_out, not_2_out, not_3_out);
  and u_addu (addu, R, instr[0], not_11_out, not_10_out, not_9_out, not_8_out, instr[5]);
  and u_subu (subu, R, instr[0], instr[1], not_10_out, not_9_out, not_8_out, instr[5]);
  and u_ori (ori, instr[26], not_6_out, instr[28], instr[29], not_2_out, not_3_out);
  and u_lw (lw, instr[26], instr[27], not_4_out, not_1_out, not_2_out, instr[31]);
  and sw (WeDm, instr[26], instr[27], not_4_out, instr[29], not_2_out, instr[31]);
  and u_beq (beq, not_5_out, not_6_out, instr[28], not_1_out, not_2_out, not_3_out);
  and u_lui (lui, instr[26], instr[27], instr[28], instr[29], not_2_out, not_3_out);
  and u_j (j, not_5_out, instr[27], not_4_out, not_1_out, not_2_out, not_3_out);
  and u_jal (jal, instr[26], instr[27], not_4_out, not_1_out, not_2_out, not_3_out);
  and u_jr (jr, R, not_12_out, not_11_out, not_10_out, instr[3], not_8_out, not_7_out);
  buf or_1 (WhichtoReg[0], lw);  // OR_Gate
  or or_2 (RegDst[0], ori, lw, lui);
  buf or_3 (RegDst[1], jal);  // OR_Gate
  buf or_4 (WhichtoReg[1], jal);  // OR_Gate
  or or_5 (AluSrc, ori, lw, WeDm, lui);
  or or_6 (WeGrf, addu, subu, lw, ori, lui, jal);
  or or_7 (AluOp[0], subu, ori, 1'b0, 1'b0);
  buf or_8 (AluOp[1], ori);  // OR_Gate
  or or_9 (AluOp[2], lui, 1'b0);
  or or_10 (sign, lw, WeDm, beq);
  and and_1 (branch, beq, eq);
  or or_11 (JType, j, jal);
  // Probe on AluOp

  // Other names for the same wires on the sheet: func[5:0] = instr[5:0]; op[5:0] = instr[31:26]; sw = WeDm

  // Notes on the sheet:
  //   Controller
  //   addu subu lw sw lui ori beq jal jr
  //   addu subu lw sw lui ori beq j jal jr
  //   addu
  //   lw
  //   sw
  //   subu
  //   000+
  //   001-
  //   andi
  //   010&
  //   ori
  //   011|
  //   100 lui
  //   00 Rd is the WriteAddr
  //   01 Rt is the WriteAddr
  //   10 31 is the WirteAddr
  //   0: reg, 1: ext(imm)
  //   00 res->Reg
  //   01 MemRead->Reg
  //   10 PC4 -> Reg
endmodule

module DataPath (
  input  clk,
  input  reset,
  input  WeGrf,
  input  WeDm,
  input  [1:0] RegDst,
  input  [1:0] WhichtoReg,
  input  AluSrc,
  input  [2:0] AluOp,
  input  sign,
  input  branch,
  input  JType,
  input  jr,
  output [31:0] instr
);

  wire AluSrcD, AluSrcE, eq, WeDmD, WeDmE, WeDmM, WeDmW, WeGrfD, WeGrfE, WeGrfM, WeGrfW;
  wire [1:0] RegDstD, undriven_2, WhichtoRegD, WhichtoRegE, WhichtoRegM, WhichtoRegW;
  wire [2:0] AluOpD, AluOpE;
  wire [4:0] RegWriteAddrD, RegWriteAddrE, RegWriteAddrM, RegWriteAddrW;
  wire [5:0] func;
  wire [25:6] imm26;
  wire [31:0] AluB, imm32D, imm32E, InstrE, InstrM, InstrW, MemReadM, MemReadW, multiplexer_1_out,
       multiplexer_2_out, multiplexer_4_out, multiplexer_6_out, NPC, PC, PcD, PcE, PcM, PcW, PcW8, RD1E,
       RD2E, RD2M, RegRead1, RegRead2, RegWrite, ResE, ResM, ResW, undriven, undriven_3, undriven_4;
  wire [31:26] InstrD;

  PC pc_1 (.clk(clk), .reset(reset), .NPC(NPC), .PC(PC));
  IM im_1 (.PC(PC), .instr(instr));
  IFID ifid_1 (.PcF(PC), .InstrF(instr), .PcD(PcD), .InstrD({InstrD, imm26, func}));  // open: clk, en, reset
  // Probe on {InstrD, imm26, func}
  EXT ext_1 (.imm16({imm26[15:6], func}), .imm32(imm32D), .sign(sign));
  Multiplexer #(.width(32), .enable("false")) multiplexer_1 (
    .in0(RegRead1), .in1(ResM), .out(multiplexer_1_out));  // open: sel
  Multiplexer #(.width(32), .enable("false")) multiplexer_2 (
    .in0(RegRead2), .in1(ResM), .out(multiplexer_2_out));  // open: sel
  Controller controller_1 (
    .AluOp(AluOpD), .WeGrf(WeGrfD), .WeDm(WeDmD), .branch(branch), .AluSrc(AluSrcD),
    .WhichtoReg(WhichtoRegD), .RegDst(RegDstD), .sign(sign), .JType(JType), .jr(jr), .instr(instr), .eq(eq));
  GRF grf_1 (
    .A1(imm26[25:21]), .A2(imm26[20:16]), .A3(RegWriteAddrW), .WD(RegWrite), .RD1(RegRead1), .RD2(RegRead2));  // open: clk, reset, WE
  Adder #(.width(32)) adder_1 (.a(PcW), .b(32'h8), .out(PcW8));  // open: cin, cout
  NPC npc_1 (
    .branch(branch), .JType(JType), .jr(jr), .PC(PC), .RegJump(RegRead1), .imm26({imm26, func}), .NPC(NPC),
    .PcD(PcD));
  Comparator #(.width(32)) comparator_1 (.a(multiplexer_1_out), .b(multiplexer_2_out), .eq(eq));  // open: gt, lt
  Multiplexer #(.select(2), .width(5), .enable("false")) multiplexer_3 (
    .in0(imm26[15:11]), .in1(imm26[20:16]), .in2({5{1'b1}}), .out(RegWriteAddrD), .sel(RegDst));  // open: in3
  IDEX idex_1 (
    .RdD(RegWriteAddrD), .PcD(PcD), .InstrD({InstrD, imm26, func}), .RD1D(RegRead1), .RD2D(RegRead2),
    .imm32D(imm32D), .RdE(RegWriteAddrE), .PcE(PcE), .InstrE(InstrE), .RD1E(RD1E), .RD2E(RD2E),
    .imm32E(imm32E), .WeGrfD(WeGrfD), .WeDmD(WeDmD), .WhichtoRegD(WhichtoRegD), .AluSrcD(AluSrcD),
    .AluOpD(AluOpD), .WeGrfE(WeGrfE), .WeDmE(WeDmE), .AluSrcE(AluSrcE), .WhichtoRegE(WhichtoRegE),
    .AluOpE(AluOpE));  // open: en, clk, reset
  Multiplexer #(.select(2), .width(32), .enable("false")) multiplexer_4 (
    .in0(RD2E), .in1(ResM), .in2(RegWrite), .in3(undriven), .out(multiplexer_4_out), .sel(undriven_2));
  Multiplexer #(.width(32), .enable("false")) multiplexer_5 (
    .in0(multiplexer_4_out), .in1(imm32E), .out(AluB), .sel(AluSrcE));
  Multiplexer #(.select(2), .width(32), .enable("false")) multiplexer_6 (
    .in0(RD1E), .in1(ResM), .in2(RegWrite), .in3(undriven_3), .out(multiplexer_6_out));  // open: sel
  ALU alu_1 (.A(multiplexer_6_out), .B(AluB), .AluOp(AluOpE), .res(ResE));
  // Probe on ResE
  // Probe on AluOpE
  EXMEM exmem_1 (
    .PcE(PcE), .InstrE(InstrE), .RdE(RegWriteAddrE), .RD2E(RD2E), .ResE(ResE), .PcM(PcM), .InstrM(InstrM),
    .RdM(RegWriteAddrM), .RD2M(RD2M), .ResM(ResM), .WeGrfE(WeGrfE), .WhichtoRegE(WhichtoRegE), .WeDmE(WeDmE),
    .WhichtoRegM(WhichtoRegM), .WeGrfM(WeGrfM), .WeDmM(WeDmM));  // open: clk, en, reset
  // Probe on ResM
  // Probe on RD2M
  DM dm_1 (.clk(clk), .reset(reset), .WD(RD2M), .RD(MemReadM), .WE(WeDm), .MemAddr(ResM));
  MEMWB memwb_1 (
    .PcM(PcM), .InstrM(InstrM), .RdM(RegWriteAddrM), .ResM(ResM), .MemReadM(MemReadM), .PcW(PcW),
    .InstrW(InstrW), .RdW(RegWriteAddrW), .ResW(ResW), .MemReadW(MemReadW), .WeGrfM(WeGrfM), .WeDmM(WeDmM),
    .WhichtoRegM(WhichtoRegM), .WeGrfW(WeGrfW), .WeDmW(WeDmW), .WhichtoRegW(WhichtoRegW));  // open: clk, en, reset
  Multiplexer #(.select(2), .width(32), .enable("false")) multiplexer_7 (
    .in0(ResW), .in1(MemReadW), .in2(undriven_4), .out(RegWrite), .sel(WhichtoRegW));  // open: in3
  // Probe on WhichtoRegW

  // Other names for the same wires on the sheet: imm26[5:0] = func; InstrD[25:0] = {imm26, func};
  //   shamt[4:0] = imm26[10:6]; rd[4:0] = imm26[15:11]; rt[4:0] = imm26[20:16]; rs[4:0] = imm26[25:21];
  //   op[5:0] = InstrD

  // Notes on the sheet:
  //   IF
  //   Datapath
  //   ID
  //   EX
  //   000+
  //   001-
  //   010&
  //   011|
  //   MEM
  //   WB
endmodule

module GRF (
  input  clk,
  input  reset,
  input  WE,
  input  [4:0] A1,
  input  [4:0] A2,
  input  [4:0] A3,
  input  [31:0] WD,
  output [31:0] RD1,
  output [31:0] RD2
);

  wire [31:0] in00, in01, in02, in03, in04, in05, in06, in07, in08, in09, in10, in11, in12, in13, in14, in15,
       in16, in17, in18, in19, in20, in21, in22, in23, in24, in25, in26, in27, in28, in29, in30, in31, out00,
       out01, out02, out03, out04, out05, out06, out07, out08, out09, out10, out11, out12, out13, out14,
       out15, out16, out17, out18, out19, out20, out21, out22, out23, out24, out25, out26, out27, out28,
       out29, out30, out31;

  // Probe on WD
  Demultiplexer #(.select(5), .width(32), .tristate("true"), .enable("false")) demultiplexer_1 (
    .out0(in00), .out1(in01), .out2(in02), .out3(in03), .out4(in04), .out5(in05), .out6(in06), .out7(in07),
    .out8(in08), .out9(in09), .out10(in10), .out11(in11), .out12(in12), .out13(in13), .out14(in14),
    .out15(in15), .out16(in16), .out17(in17), .out18(in18), .out19(in19), .out20(in20), .out21(in21),
    .out22(in22), .out23(in23), .out24(in24), .out25(in25), .out26(in26), .out27(in27), .out28(in28),
    .out29(in29), .out30(in30), .out31(in31), .in(WD), .sel(A3));
  // Probe on A3
  Register #(.width(32)) register_1 (.D(in00), .Q(out00), .clr(1'b1));  // open: en, clk
  Register #(.width(32)) register_2 (.D(in08), .en(WE), .Q(out08), .clk(clk), .clr(reset));
  Register #(.width(32)) register_3 (.D(in16), .en(WE), .Q(out16), .clk(clk), .clr(reset));
  Register #(.width(32)) register_4 (.D(in24), .en(WE), .Q(out24), .clk(clk), .clr(reset));
  Register #(.width(32)) register_5 (.D(in01), .en(WE), .Q(out01), .clk(clk), .clr(reset));
  Register #(.width(32)) register_6 (.D(in09), .en(WE), .Q(out09), .clk(clk), .clr(reset));
  Register #(.width(32)) register_7 (.D(in17), .en(WE), .Q(out17), .clk(clk), .clr(reset));
  Register #(.width(32)) register_8 (.D(in25), .en(WE), .Q(out25), .clk(clk), .clr(reset));
  Multiplexer #(.select(5), .width(32), .enable("false")) multiplexer_1 (
    .in0(out00), .in1(out01), .in2(out02), .in3(out03), .in4(out04), .in5(out05), .in6(out06), .in7(out07),
    .in8(out08), .in9(out09), .in10(out10), .in11(out11), .in12(out12), .in13(out13), .in14(out14),
    .in15(out15), .in16(out16), .in17(out17), .in18(out18), .in19(out19), .in20(out20), .in21(out21),
    .in22(out22), .in23(out23), .in24(out24), .in25(out25), .in26(out26), .in27(out27), .in28(out28),
    .in29(out29), .in30(out30), .in31(out31), .out(RD1), .sel(A1));
  Register #(.width(32)) register_9 (.D(in02), .en(WE), .Q(out02), .clk(clk), .clr(reset));
  Register #(.width(32)) register_10 (.D(in10), .en(WE), .Q(out10), .clk(clk), .clr(reset));
  Register #(.width(32)) register_11 (.D(in18), .en(WE), .Q(out18), .clk(clk), .clr(reset));
  Register #(.width(32)) register_12 (.D(in26), .en(WE), .Q(out26), .clk(clk), .clr(reset));
  Register #(.width(32)) register_13 (.D(in03), .en(WE), .Q(out03), .clk(clk), .clr(reset));
  Register #(.width(32)) register_14 (.D(in11), .en(WE), .Q(out11), .clk(clk), .clr(reset));
  Register #(.width(32)) register_15 (.D(in19), .en(WE), .Q(out19), .clk(clk), .clr(reset));
  Register #(.width(32)) register_16 (.D(in27), .en(WE), .Q(out27), .clk(clk), .clr(reset));
  Register #(.width(32)) register_17 (.D(in04), .en(WE), .Q(out04), .clk(clk), .clr(reset));
  Register #(.width(32)) register_18 (.D(in12), .en(WE), .Q(out12), .clk(clk), .clr(reset));
  Register #(.width(32)) register_19 (.D(in20), .en(WE), .Q(out20), .clk(clk), .clr(reset));
  Register #(.width(32)) register_20 (.D(in28), .en(WE), .Q(out28), .clk(clk), .clr(reset));
  Multiplexer #(.select(5), .width(32), .enable("false")) multiplexer_2 (
    .in0(out00), .in1(out01), .in2(out02), .in3(out03), .in4(out04), .in5(out05), .in6(out06), .in7(out07),
    .in8(out08), .in9(out09), .in10(out10), .in11(out11), .in12(out12), .in13(out13), .in14(out14),
    .in15(out15), .in16(out16), .in17(out17), .in18(out18), .in19(out19), .in20(out20), .in21(out21),
    .in22(out22), .in23(out23), .in24(out24), .in25(out25), .in26(out26), .in27(out27), .in28(out28),
    .in29(out29), .in30(out30), .in31(out31), .out(RD2), .sel(A2));
  Register #(.width(32)) register_21 (.D(in05), .en(WE), .Q(out05), .clk(clk), .clr(reset));
  Register #(.width(32)) register_22 (.D(in13), .en(WE), .Q(out13), .clk(clk), .clr(reset));
  Register #(.width(32)) register_23 (.D(in21), .en(WE), .Q(out21), .clk(clk), .clr(reset));
  Register #(.width(32)) register_24 (.D(in29), .en(WE), .Q(out29), .clk(clk), .clr(reset));
  Register #(.width(32)) register_25 (.D(in06), .en(WE), .Q(out06), .clk(clk), .clr(reset));
  Register #(.width(32)) register_26 (.D(in14), .en(WE), .Q(out14), .clk(clk), .clr(reset));
  Register #(.width(32)) register_27 (.D(in22), .en(WE), .Q(out22), .clk(clk), .clr(reset));
  Register #(.width(32)) register_28 (.D(in30), .en(WE), .Q(out30), .clk(clk), .clr(reset));
  Register #(.width(32)) register_29 (.D(in07), .en(WE), .Q(out07), .clk(clk), .clr(reset));
  Register #(.width(32)) register_30 (.D(in15), .en(WE), .Q(out15), .clk(clk), .clr(reset));
  Register #(.width(32)) register_31 (.D(in23), .en(WE), .Q(out23), .clk(clk), .clr(reset));
  Register #(.width(32)) register_32 (.D(in31), .en(WE), .Q(out31), .clk(clk), .clr(reset));

  // Notes on the sheet:
  //   Global Register File
endmodule

module ALU (
  input  [31:0] A,
  input  [31:0] B,
  input  [2:0] AluOp,
  output [31:0] res
);

  wire [31:0] adder_1_out, and_1_out, or_1_out, subtractor_1_out;

  Adder #(.width(32)) adder_1 (.a(A), .b(B), .out(adder_1_out));  // open: cin, cout
  Subtractor #(.width(32)) subtractor_1 (.a(A), .b(B), .out(subtractor_1_out));  // open: bin, bout
  assign and_1_out = A & B;  // AND_Gate and_1, 32 bits wide
  assign or_1_out = A | B;  // OR_Gate or_1, 32 bits wide
  // Probe on A
  // Probe on B
  // Probe on res
  Multiplexer #(.select(3), .width(32), .enable("false")) multiplexer_1 (
    .in0(adder_1_out), .in1(subtractor_1_out), .in2(and_1_out), .in3(or_1_out), .in4({B[15:0], {16{1'b0}}}),
    .out(res), .sel(AluOp));  // open: in5, in6, in7

  // Notes on the sheet:
  //   Arithmetic and Logic Unit
  //   000+
  //   001-
  //   010&
  //   011|
  //   100 lui
endmodule

module EXT (
  input  [15:0] imm16,
  input  sign,
  output [31:0] imm32
);

  wire [31:0] bit_extender_1_out, bit_extender_2_out;

  assign bit_extender_1_out = {{16{1'b0}}, imm16};  // Bit_Extender bit_extender_1
  assign bit_extender_2_out = {{16{imm16[15]}}, imm16};  // Bit_Extender bit_extender_2
  Multiplexer #(.width(32), .enable("false")) multiplexer_1 (
    .in0(bit_extender_1_out), .in1(bit_extender_2_out), .out(imm32), .sel(sign));
endmodule

module DM (
  input  clk,
  input  reset,
  input  WE,
  input  [31:0] MemAddr,
  input  [31:0] WD,
  output [31:0] RD
);

  // Probe on MemAddr[11:2]
  // Probe on WD
  RAM #(.addrWidth(10), .dataWidth(32), .bus("separate")) ram_1 (
    .addr(MemAddr[11:2]), .din(WD), .data(RD), .str(WE), .clk(clk), .clr(reset));  // open: sel, ld

  // Notes on the sheet:
  //   but mips address by byte(8 bits)
  //   Data Memory
  //   addressing by word(32 bits)
endmodule

module PC (
  input  clk,
  input  reset,
  input  [31:0] NPC,
  output [31:0] PC
);

  wire comparator_1_eq;
  wire [31:0] multiplexer_1_out, PC_q;

  // Probe on NPC
  Multiplexer #(.width(32), .enable("false")) multiplexer_1 (
    .in0(NPC), .in1(32'h3000), .out(multiplexer_1_out), .sel(reset));
  Register #(.width(32)) u_PC (.D(multiplexer_1_out), .Q(PC_q), .clk(clk));  // open: en, clr
  Comparator #(.width(32)) comparator_1 (.a(PC_q), .b({32{1'b0}}), .eq(comparator_1_eq));  // open: gt, lt
  Multiplexer #(.width(32), .enable("false")) multiplexer_2 (
    .in0(PC_q), .in1(32'h3000), .out(PC), .sel(comparator_1_eq));
endmodule

module NPC (
  input  branch,
  input  JType,
  input  jr,
  input  [31:0] PC,
  input  [31:0] PcD,
  input  [31:0] RegJump,
  input  [25:0] imm26,
  output [31:0] NPC
);

  wire [31:0] bit_extender_1_out, multiplexer_1_out, multiplexer_2_out, PC4, PcBranch, PcD4, shifter_1_out;

  // Probe on PC
  // Probe on PcD
  Multiplexer #(.width(32), .enable("false")) multiplexer_1 (
    .in0(PC4), .in1(PcBranch), .out(multiplexer_1_out), .sel(branch));
  assign bit_extender_1_out = {{16{imm26[15]}}, imm26[15:0]};  // Bit_Extender bit_extender_1
  Shifter #(.width(32)) shifter_1 (.in(bit_extender_1_out), .\dist (5'b00010), .out(shifter_1_out));
  Multiplexer #(.width(32), .enable("false")) multiplexer_2 (
    .in0(multiplexer_1_out), .in1({PcD4[31:28], imm26, 2'b00}), .out(multiplexer_2_out), .sel(JType));
  Adder #(.width(32)) adder_1 (.a(shifter_1_out), .b(PcD4), .out(PcBranch));  // open: cin, cout
  Adder #(.width(32)) adder_2 (.a(PC), .b(32'h4), .out(PC4));  // open: cin, cout
  Adder #(.width(32)) adder_3 (.a(PcD), .b(32'h4), .out(PcD4));  // open: cin, cout
  // Probe on NPC
  Multiplexer #(.width(32), .enable("false")) multiplexer_3 (
    .in0(multiplexer_2_out), .in1(RegJump), .out(NPC), .sel(jr));

  // Other names for the same wires on the sheet: PcJ[31:2] = {PcD4[31:28], imm26}; PcJr[31:0] = RegJump

  // Notes on the sheet:
  //   NPC
endmodule

module IM (
  input  [31:0] PC,
  output [31:0] instr
);

  wire [31:0] subtractor_1_out;

  Subtractor #(.width(32)) subtractor_1 (.a(PC), .b(32'h3000), .out(subtractor_1_out));  // open: bin, bout
  ROM #(.addrWidth(10), .dataWidth(32)) rom_1 (.addr(subtractor_1_out[11:2]), .data(instr));  // open: sel

  // Notes on the sheet:
  //   IM
  //   contents of rom_1 (hex, n*v repeats v):
  //   34040100 34850123 3c0601c8 3c07ffff 34e7ffff 868021 878821 e7a021 869023 879823 ac040000 ac050004
  //   ac060008 ac07000c ac100010 ac110014 ac120018 ac13002c ac140030 8c040000 8c05000c ac04001c ac050020
  //   34040001 34050002 34060001 10850001 10860001 ad040024 ad050028 c000c23 c000c23 ad150040 34a50004
  //   c000c27 ad050038 ad1f003c 36b50005 3e00008 ad050044 ad1f0048
endmodule

module IFID (
  input  clk,
  input  en,
  input  reset,
  input  [31:0] PcF,
  input  [31:0] InstrF,
  output [31:0] PcD,
  output [31:0] InstrD
);

  Register #(.width(32)) PC (.D(PcF), .en(en), .Q(PcD), .clk(clk), .clr(reset));
  Register #(.width(32)) PC_2 ();  // open: D, en, Q, clk, clr
  Register #(.width(32)) instr (.D(InstrF), .en(en), .Q(InstrD), .clk(clk), .clr(reset));

  // Notes on the sheet:
  //   IFID
endmodule

module IDEX (
  input  en,
  input  clk,
  input  reset,
  input  [4:0] RdD,
  input  [31:0] PcD,
  input  [31:0] InstrD,
  input  [31:0] RD1D,
  input  [31:0] RD2D,
  input  [31:0] imm32D,
  input  WeGrfD,
  input  WeDmD,
  input  [1:0] WhichtoRegD,
  input  AluSrcD,
  input  [2:0] AluOpD,
  output [4:0] RdE,
  output [31:0] PcE,
  output [31:0] InstrE,
  output [31:0] RD1E,
  output [31:0] RD2E,
  output [31:0] imm32E,
  output WeGrfE,
  output WeDmE,
  output [1:0] WhichtoRegE,
  output AluSrcE,
  output [2:0] AluOpE
);

  Register #(.width(32)) PC (.D(PcD), .en(en), .Q(PcE), .clk(clk), .clr(reset));
  Register #(.width(32)) RD1 (.D(RD1D), .en(en), .Q(RD1E), .clk(clk), .clr(reset));
  Register #(.width(32)) imm32 (.D(imm32D), .en(en), .Q(imm32E), .clk(clk), .clr(reset));
  Register #(.width(1)) WeGrf (.D(WeGrfD), .en(en), .Q(WeGrfE), .clk(clk), .clr(reset));
  Register #(.width(1)) AluSrc (.D(AluSrcD), .en(en), .Q(AluSrcE), .clk(clk), .clr(reset));
  Register #(.width(32)) PC_2 ();  // open: D, en, Q, clk, clr
  Register #(.width(32)) instr (.D(InstrD), .en(en), .Q(InstrE), .clk(clk), .clr(reset));
  Register #(.width(32)) RD2 (.D(RD2D), .en(en), .Q(RD2E), .clk(clk), .clr(reset));
  Register #(.width(1)) WeDm (.D(WeDmD), .en(en), .Q(WeDmE), .clk(clk), .clr(reset));
  Register #(.width(3)) AluOp (.D(AluOpD), .en(en), .Q(AluOpE), .clk(clk), .clr(reset));
  Register #(.width(5)) rd (.D(RdD), .en(en), .Q(RdE), .clk(clk), .clr(reset));
  Register #(.width(2)) WhichtoReg (.D(WhichtoRegD), .en(en), .Q(WhichtoRegE), .clk(clk), .clr(reset));

  // Notes on the sheet:
  //   IDEX
endmodule

module EXMEM (
  input  clk,
  input  en,
  input  reset,
  input  [31:0] PcE,
  input  [31:0] InstrE,
  input  [4:0] RdE,
  input  [31:0] RD2E,
  input  [31:0] ResE,
  input  WeGrfE,
  input  WeDmE,
  input  [1:0] WhichtoRegE,
  output [31:0] PcM,
  output [31:0] InstrM,
  output [4:0] RdM,
  output [31:0] RD2M,
  output [31:0] ResM,
  output WeGrfM,
  output WeDmM,
  output [1:0] WhichtoRegM
);

  Register #(.width(32)) PC (.D(PcE), .en(en), .Q(PcM), .clk(clk), .clr(reset));
  Register #(.width(32)) res (.D(ResE), .en(en), .Q(ResM), .clk(clk), .clr(reset));
  Register #(.width(32)) RD2 (.D(RD2E), .en(en), .Q(RD2M), .clk(clk), .clr(reset));
  Register #(.width(1)) WeGrf (.D(WeGrfE), .en(en), .Q(WeGrfM), .clk(clk), .clr(reset));
  Register #(.width(5)) rd (.D(RdE), .en(en), .Q(RdM), .clk(clk), .clr(reset));
  Register #(.width(1)) WeDm (.D(WeDmE), .en(en), .Q(WeDmM), .clk(clk), .clr(reset));
  Register #(.width(32)) PC_2 ();  // open: D, en, Q, clk, clr
  Register #(.width(32)) instr (.D(InstrE), .en(en), .Q(InstrM), .clk(clk), .clr(reset));
  Register #(.width(2)) WhichtoReg (.D(WhichtoRegE), .en(en), .Q(WhichtoRegM), .clk(clk), .clr(reset));

  // Notes on the sheet:
  //   EXMEM
endmodule

module MEMWB (
  input  clk,
  input  en,
  input  reset,
  input  [31:0] PcM,
  input  [31:0] InstrM,
  input  [4:0] RdM,
  input  [31:0] ResM,
  input  [31:0] MemReadM,
  input  WeGrfM,
  input  WeDmM,
  input  [1:0] WhichtoRegM,
  output [31:0] PcW,
  output [31:0] InstrW,
  output [4:0] RdW,
  output [31:0] ResW,
  output [31:0] MemReadW,
  output WeGrfW,
  output WeDmW,
  output [1:0] WhichtoRegW
);

  Register #(.width(32)) PC (.D(PcM), .en(en), .Q(PcW), .clk(clk), .clr(reset));
  Register #(.width(32)) res (.D(ResM), .en(en), .Q(ResW), .clk(clk), .clr(reset));
  Register #(.width(1)) WeGrf (.D(WeGrfM), .en(en), .Q(WeGrfW), .clk(clk), .clr(reset));
  Register #(.width(32)) MemRead (.D(MemReadM), .en(en), .Q(MemReadW), .clk(clk), .clr(reset));
  Register #(.width(5)) rd (.D(RdM), .en(en), .Q(RdW), .clk(clk), .clr(reset));
  Register #(.width(32)) PC_2 ();  // open: D, en, Q, clk, clr
  Register #(.width(32)) instr (.D(InstrM), .en(en), .Q(InstrW), .clk(clk), .clr(reset));
  Register #(.width(1)) WeDm (.D(WeDmM), .en(en), .Q(WeDmW), .clk(clk), .clr(reset));
  Register #(.width(2)) WhichtoReg (.D(WhichtoRegM), .en(en), .Q(WhichtoRegW), .clk(clk), .clr(reset));

  // Notes on the sheet:
  //   MEMWB
endmodule
